// Digital circuit TD4-Sim.dig as structural Verilog
module TD4_Sim (
  input  clk,
  output out_1,
  output out_2,
  output out_3,
  output out_4,
  output out_6,
  output out_7,
  output out_8,
  output out_9,
  output out_10,
  output out_11,
  output out_12,
  output out_13
);

  wire _74283_1_pin9, BUS_b0, BUS_b1, BUS_b2, BUS_b3, CARRY, D0, D1, D2, D3, D4, D5, D6, D7, IN0, IN1, IN2,
       IN3, LD_OUT, LD_PC, LD_REGA, LD_REGB, nand_1_out, or_2_out, RESET, SELA, SRC0, SRC1, SRC2, SRC3;
  wire [3:0] ADDR;

  _74161 _74161_1 (
    .pin1(RESET), .pin2(clk), .pin3(BUS_b0), .pin4(BUS_b1), .pin5(BUS_b2), .pin6(BUS_b3), .pin7(1'b0),
    .pin8(1'b0), .pin9(LD_REGA), .pin10(1'b0), .pin11(out_6), .pin12(out_7), .pin13(out_8), .pin14(out_9),
    .pin16(1'b1));  // open: pin15
  _74161 _74161_2 (
    .pin1(RESET), .pin2(clk), .pin3(BUS_b0), .pin4(BUS_b1), .pin5(BUS_b2), .pin6(BUS_b3), .pin7(1'b0),
    .pin8(1'b0), .pin9(LD_REGB), .pin10(1'b0), .pin11(out_10), .pin12(out_11), .pin13(out_12),
    .pin14(out_13), .pin16(1'b1));  // open: pin15
  _74161 _74161_3 (
    .pin1(RESET), .pin2(clk), .pin3(BUS_b0), .pin4(BUS_b1), .pin5(BUS_b2), .pin6(BUS_b3), .pin7(1'b0),
    .pin8(1'b0), .pin9(LD_OUT), .pin10(1'b0), .pin11(out_4), .pin12(out_3), .pin13(out_2), .pin14(out_1),
    .pin16(1'b1));  // open: pin15
  _74161 _74161_4 (
    .pin1(RESET), .pin2(clk), .pin3(BUS_b0), .pin4(BUS_b1), .pin5(BUS_b2), .pin6(BUS_b3), .pin7(1'b1),
    .pin8(1'b0), .pin9(LD_PC), .pin10(1'b1), .pin11(ADDR[3]), .pin12(ADDR[2]), .pin13(ADDR[1]),
    .pin14(ADDR[0]), .pin16(1'b1));  // open: pin15
  DipSwitch dipswitch_1 (.out(IN3));
  DipSwitch dipswitch_2 (.out(IN2));
  DipSwitch dipswitch_3 (.out(IN1));
  DipSwitch dipswitch_4 (.out(RESET));
  DipSwitch dipswitch_5 (.out(IN0));
  _74153 _74153_1 (
    .pin1(1'b0), .pin2(D5), .pin3(1'b0), .pin4(IN0), .pin5(out_13), .pin6(out_9), .pin7(SRC0), .pin8(1'b0),
    .pin9(SRC1), .pin10(out_8), .pin11(out_12), .pin12(IN1), .pin13(1'b0), .pin14(SELA), .pin15(1'b0),
    .pin16(1'b1));
  _74153 _74153_2 (
    .pin1(1'b0), .pin2(D5), .pin3(1'b0), .pin4(IN2), .pin5(out_11), .pin6(out_7), .pin7(SRC2), .pin8(1'b0),
    .pin9(SRC3), .pin10(out_6), .pin11(out_10), .pin12(IN3), .pin13(1'b0), .pin14(SELA), .pin15(1'b0),
    .pin16(1'b1));
  or or_1 (SELA, D4, D7);
  nand nand_1 (nand_1_out, 1'b1, 1'b1, D6);
  or or_2 (or_2_out, CARRY, D4);
  or or_3 (LD_REGA, D6, D7);
  or or_4 (LD_REGB, nand_1_out, D7);
  nand nand_2 (LD_OUT, 1'b1, nand_1_out, D7);
  nand nand_3 (LD_PC, D6, D7, or_2_out);
  _74283 _74283_1 (
    .pin1(BUS_b1), .pin2(SRC1), .pin3(D1), .pin4(BUS_b0), .pin5(D0), .pin6(SRC0), .pin7(1'b0), .pin8(1'b0),
    .pin9(_74283_1_pin9), .pin10(BUS_b3), .pin11(SRC3), .pin12(D3), .pin13(BUS_b2), .pin14(SRC2), .pin15(D2),
    .pin16(1'b1));
  _7474 _7474_1 (
    .pin1(1'b0), .pin2(1'b0), .pin3(1'b0), .pin4(1'b0), .pin7(1'b0), .pin8(CARRY), .pin10(1'b1), .pin11(clk),
    .pin12(_74283_1_pin9), .pin13(RESET), .pin14(1'b1));  // open: pin5, pin6, pin9
  ROM #(.AddrBits(4), .Bits(8)) rom_1 (.A(ADDR), .sel(1'b1), .D({D7, D6, D5, D4, D3, D2, D1, D0}));

  // Other names for the same wires on the sheet: SELB = D5; CLOCK = clk; REGA_b0 = out_9; REGA_b1 = out_8;
  //   REGA_b2 = out_7; REGA_b3 = out_6; REGB_b0 = out_13; REGB_b1 = out_12; REGB_b2 = out_11; REGB_b3 = out_10

  // Notes on the sheet:
  //   clk: Hz: 10
  //   contents of rom_1 (hex, n*v repeats v):
  //   a1,1,a2,51,a4,1,a8,51,a4,1,a2,51,f0
endmodule
